# Fritzing sketch PROJECTLT (saved by Fritzing 0.9.3b)
circuit board: 11.6605cm x 6.53389cm
breadboards: 1

parts:
  Part1 = Arduino Uno (Rev3) - ICSP
  Part2 = Gas Sensor Breakout Board
  Mod1 = KY-028 Digital Temperature Sensor Module [package="Breakout board"]
  LED1 = smd LED [color="Red (633nm)" package="1206 [SMD]"]
  R1 = Resistor [tolerance=±5% resistance=220 package="0805 [SMD]"]
  DHT1 = DHT11 Humitidy and Temperature Sensor
  J1 = Piezo Speaker

nets:
  N1: Part1.A1, Part2.A1
  N2: Part1.A4/SDA, Part2.B1
  N3: Part1.A5/SCL, Mod1.A0
  N4: Part1.5V, Mod1.+
  GND: Part1.GND, Part2.GND, Mod1.G, LED1.cathode, DHT1.GND, J1.pin1
  N5: Part1.D11_PWM/MOSI, R1.Pin_1
  N6: Part1.D12/MISO, Mod1.D0
  N7: Part1.D13/SCK, J1.pin2
  N8: Part1.D4, DHT1.DATA
  3V3: Part1.3V3, DHT1.VDD
  N9: LED1.anode, R1.Pin_0

custom parts:
  KY-028 Digital Temperature Sensor Module: KY-028 Digital Temperature Sensor Module, used to measure changes in temperature.
  DHT11 Humitidy and Temperature Sensor: DHT11 Humidity and Temperature Sensor
